# Fritzing sketch cpc-templight (saved by Fritzing 0.7.3b)
breadboards: 1

parts:
  LED1 = RGB LED (com. anode, rbg) [package="5 mm [THT]"]
  T1 = LM34 Temperature Sensor [package="TO92 [THT]"]
  Arduino1 = Arduino
  R1 = Resistor [tolerance=±5% resistance=270 package=THT]
  R2 = Resistor [tolerance=±5% resistance=270 package=THT]
  R3 = Resistor [tolerance=±5% resistance=270 package=THT]

nets (from the schematic view):
  N1: LED1.red_cathode, R1.Pin_0
  N2: LED1.common_anode, T1.+Vs, Arduino1.+5V
  N3: LED1.blue_cathode, R2.Pin_0
  N4: LED1.green_cathode, R3.Pin_0
  N5: T1.Vout, Arduino1.A0
  GND: T1.GND, Arduino1.GND
  N6: Arduino1.D6, R2.Pin_1
  N7: Arduino1.D5, R3.Pin_1
  N8: Arduino1.D3, R1.Pin_1
