# Fritzing sketch arduino-flasher-shield (saved by Fritzing 0.7.0b)
breadboards: 1

parts:
  Arduino1 = Arduino
  28W_ZIF_SOCKET = atmega168 [package="DIP28 [THT]"]
  J1 = female pin header, 3 pins [form="♀ (female)"]
  TX = female pin header, 2 pins [form="♀ (female)"]
  RX = female pin header, 2 pins [form="♀ (female)"]
  22pF = Ceramic Capacitor [capacitance=22pF package="100 mil [THT, multilayer]"]
  22pF_2 = Ceramic Capacitor [capacitance=22pF package="100 mil [THT, multilayer]"]
  16MHz = Crystal [frequency="16 Mhz" package=THT]
  10K = Resistor [tolerance=±5% resistance=10k package=THT]

nets:
  N1: Arduino1.D13, 28W_ZIF_SOCKET.Pin_19
  N2: Arduino1.D12, 28W_ZIF_SOCKET.Pin_18
  N3: Arduino1.D11, 28W_ZIF_SOCKET.Pin_17
  N4: Arduino1.D10, J1.pin1
  N5: Arduino1.D1TX, TX.pin1
  N6: Arduino1.D0RX, RX.pin1
  N7: Arduino1.RST, J1.pin3
  N8: Arduino1.+5V, 28W_ZIF_SOCKET.Pin_7, 28W_ZIF_SOCKET.Pin_20, 10K.Pin_0
  N9: Arduino1.GND, 28W_ZIF_SOCKET.Pin_8, 28W_ZIF_SOCKET.Pin_22, 22pF.1, 22pF_2.0
  N10: 28W_ZIF_SOCKET.Pin_1, J1.pin2, 10K.Pin_1
  N11: 28W_ZIF_SOCKET.Pin_2, RX.pin2
  N12: 28W_ZIF_SOCKET.Pin_3, TX.pin2
  N13: 28W_ZIF_SOCKET.Pin_9, 22pF.0, 16MHz.pin_1
  N14: 28W_ZIF_SOCKET.Pin_10, 22pF_2.1, 16MHz.pin_0

notes:
  BTLDR
  SKETCH
  RESET
  Arduino Burner v0.1 / gareth.halfacree.co.uk
