# Fritzing sketch barebonesduino (saved by Fritzing 0.7.0b)
breadboards: 1

parts:
  U1 = atmega168 [package="DIP28 [THT]"]
  U2 = Voltage Regulator - 5V [package="TO220 [THT]"]
  C1 = Electrolytic Capacitor [capacitance=10µF package="100 mil [THT, electrolytic]"]
  C2 = Electrolytic Capacitor [capacitance=10µF package="100 mil [THT, electrolytic]"]
  LED1 = LED - 3mm [color="Red (633nm)" package="3 mm [THT]"]
  R1 = Resistor [tolerance=±5% resistance=220 package=THT]
  Power_plug1 = Power plug

nets:
  N1: U1.Pin_7, U1.Pin_20, U2.output_voltage, C2.+, R1.Pin_0, Power_plug1.VCC
  GND: U1.Pin_8, U1.Pin_22, U2.GND, C1.-, C2.-, LED1.anode, Power_plug1.GND
  N2: U2.input_voltage, C1.+
  N3: LED1.cathode, R1.Pin_1
