# Fritzing sketch ledsketch (saved by Fritzing 0.7.3b)
breadboards: 1

parts:
  R1 = Resistor [tolerance=±5% resistance=10k package=THT]
  S1 = Pushbutton [package="[THT]"]

nets:
  N1: R1.Pin_1, S1.Pin_3, S1.Pin_4
  N2: S1.Pin_1, S1.Pin_2
