# Fritzing sketch prosleepduino (saved by Fritzing 0.7.0b)
breadboards: 1

parts:
  ATMega328 = atmega168 [package="DIP28 [THT]"]
  5V_REG = Voltage Regulator - 5V [package="TO220 [THT]"]
  10µF = Electrolytic Capacitor [capacitance=10µF package="100 mil [THT, electrolytic]"]
  10µF_2 = Electrolytic Capacitor [capacitance=10µF package="100 mil [THT, electrolytic]"]
  PWR_LED = LED - 3mm [color="Red (633nm)" package="3 mm [THT]"]
  R1 = Resistor [tolerance=±5% resistance=220 package=THT]
  POWER = Power plug
  LED = Super Flux RGB LED (com. cathode)
  220 = Resistor [tolerance=±5% resistance=220 package=THT]
  220_2 = Resistor [tolerance=±5% resistance=220 package=THT]
  220_3 = Resistor [tolerance=±5% resistance=220 package=THT]
  SPEAKER = Piezo Speaker
  VOLUME = Rotary Potentiometer (Small) [maximum_resistance=100kΩ]

nets:
  N1: ATMega328.Pin_4, 220.Pin_0
  N2: ATMega328.Pin_5, 220_2.Pin_0
  N3: ATMega328.Pin_6, 220_3.Pin_0
  N4: ATMega328.Pin_7, ATMega328.Pin_20, 5V_REG.output_voltage, 10µF_2.+, R1.Pin_0
  N5: ATMega328.Pin_8, ATMega328.Pin_22, PWR_LED.anode, SPEAKER.pin1, VOLUME.leg2
  N6: ATMega328.Pin_11, VOLUME.leg1
  N7: 5V_REG.input_voltage, 10µF.+, POWER.VCC
  GND: 5V_REG.GND, 10µF.-, 10µF_2.-, POWER.GND, LED.common_cathode
  N8: PWR_LED.cathode, R1.Pin_1
  N9: LED.red_anode, 220.Pin_1
  N10: LED.blue_anode, 220_2.Pin_1
  N11: LED.green_anode, 220_3.Pin_1
  N12: SPEAKER.pin2, VOLUME.wiper
