# Fritzing sketch sleepduino-standalone (saved by Fritzing 0.7.0b)
breadboards: 2

parts:
  LED3 = Pirahna Super Flux RGB LED (Oomlout)
  LED1 = Pirahna Super Flux RGB LED (Oomlout)
  R1 = Resistor [tolerance=±5% resistance=220 package=THT]
  R4 = Resistor [tolerance=±5% resistance=220 package=THT]
  R5 = Resistor [tolerance=±5% resistance=220 package=THT]
  R6 = Resistor [tolerance=±5% resistance=220 package=THT]
  R7 = Resistor [tolerance=±5% resistance=220 package=THT]
  R8 = Resistor [tolerance=±5% resistance=220 package=THT]
  R9 = Resistor [tolerance=±5% resistance=220 package=THT]
  VOL = Rotary Potentiometer (Small) [maximum_resistance=100kΩ]
  SPK = Piezo Speaker
  BTN1 = Pushbutton [package="[THT]"]
  BTN2 = Pushbutton [package="[THT]"]
  BTN3 = Pushbutton [package="[THT]"]
  R3 = Resistor [tolerance=±5% resistance=220 package=THT]
  R2 = Resistor [tolerance=±5% resistance=220 package=THT]
  LED2 = Pirahna Super Flux RGB LED (Oomlout)
  U1 = atmega168 [package="DIP28 [THT]"]
  USB = USB connector [package=THT]

nets:
  N1: LED3.Common_Anode, LED1.Common_Anode, LED2.Common_Anode, U1.Pin_7, U1.Pin_20, USB.5V
  N2: LED3.Red_Cathode, R1.Pin_0
  N3: LED3.Blue_Cathode, R3.Pin_0
  N4: LED3.Green_Cathode, R2.Pin_0
  N5: LED1.Red_Cathode, R7.Pin_0
  N6: LED1.Blue_Cathode, R9.Pin_0
  N7: LED1.Green_Cathode, R8.Pin_0
  N8: R1.Pin_1, U1.Pin_2
  N9: R4.Pin_0, LED2.Red_Cathode
  N10: R4.Pin_1, U1.Pin_5
  N11: R5.Pin_0, LED2.Green_Cathode
  N12: R5.Pin_1, U1.Pin_6
  N13: R6.Pin_0, LED2.Blue_Cathode
  N14: R6.Pin_1, U1.Pin_11
  N15: R7.Pin_1, U1.Pin_12
  N16: R8.Pin_1, U1.Pin_13
  N17: R9.Pin_1, U1.Pin_14
  N18: VOL.leg1, SPK.pin1, BTN1.Pin_1, BTN1.Pin_2, BTN2.Pin_1, BTN2.Pin_2, BTN3.Pin_1, BTN3.Pin_2, U1.Pin_8, U1.Pin_22, USB.GND, USB.chassis5, USB.chassis6
  N19: VOL.wiper, SPK.pin2
  N20: VOL.leg2, U1.Pin_18
  N21: BTN1.Pin_3, BTN1.Pin_4, U1.Pin_15
  N22: BTN2.Pin_3, BTN2.Pin_4, U1.Pin_16
  N23: BTN3.Pin_3, BTN3.Pin_4, U1.Pin_17
  N24: R3.Pin_1, U1.Pin_4
  N25: R2.Pin_1, U1.Pin_3

notes:
  Sleepduino Standalone v0.1
  gareth.halfacree.co.uk

custom parts:
  Pirahna Super Flux RGB LED (Oomlout): A full color SuperFlux LED.
