# Fritzing sketch sleepduino (saved by Fritzing 0.7.0b)
breadboards: 1

parts:
  LED1 = Super Flux RGB LED (com. cathode)
  LED2 = Super Flux RGB LED (com. cathode)
  LED3 = Super Flux RGB LED (com. cathode)
  R1 = Resistor [tolerance=±5% resistance=220 package=THT]
  R2 = Resistor [tolerance=±5% resistance=220 package=THT]
  R3 = Resistor [tolerance=±5% resistance=220 package=THT]
  R4 = Resistor [tolerance=±5% resistance=220 package=THT]
  R5 = Resistor [tolerance=±5% resistance=220 package=THT]
  R6 = Resistor [tolerance=±5% resistance=220 package=THT]
  R7 = Resistor [tolerance=±5% resistance=220 package=THT]
  R8 = Resistor [tolerance=±5% resistance=220 package=THT]
  R9 = Resistor [tolerance=±5% resistance=220 package=THT]
  PIEZO = Piezo Speaker
  Arduino = Arduino

nets:
  N1: LED1.red_anode, R2.Pin_0
  N2: LED1.blue_anode, R1.Pin_0
  N3: LED1.green_anode, R3.Pin_0
  N4: LED1.common_cathode, LED2.common_cathode, LED3.common_cathode, Arduino.+5V
  N5: LED2.red_anode, R5.Pin_0
  N6: LED2.blue_anode, R7.Pin_0
  N7: LED2.green_anode, R8.Pin_0
  N8: LED3.red_anode, R9.Pin_0
  N9: LED3.blue_anode, R4.Pin_0
  N10: LED3.green_anode, R6.Pin_0
  N11: R1.Pin_1, Arduino.D3
  N12: R2.Pin_1, Arduino.D4
  N13: R3.Pin_1, Arduino.D2
  N14: R4.Pin_1, Arduino.D9
  N15: R5.Pin_1, Arduino.D7
  N16: R6.Pin_1, Arduino.D8
  N17: R7.Pin_1, Arduino.D6
  N18: R8.Pin_1, Arduino.D5
  N19: R9.Pin_1, Arduino.D10
  N20: PIEZO.pin1, Arduino.GND
  N21: PIEZO.pin2, Arduino.D11

notes:
  Sleepduino v0.1A
  gareth.halfacree.co.uk
