# Fritzing sketch sleepduino2 (saved by Fritzing 0.7.0b)
breadboards: 1

parts:
  LED1 = Pirahna Super Flux RGB LED (Oomlout)
  LED2 = Pirahna Super Flux RGB LED (Oomlout)
  R1 = Resistor [tolerance=±5% resistance=220 package=THT]
  R4 = Resistor [tolerance=±5% resistance=220 package=THT]
  R5 = Resistor [tolerance=±5% resistance=220 package=THT]
  R6 = Resistor [tolerance=±5% resistance=220 package=THT]
  R7 = Resistor [tolerance=±5% resistance=220 package=THT]
  R8 = Resistor [tolerance=±5% resistance=220 package=THT]
  R9 = Resistor [tolerance=±5% resistance=220 package=THT]
  VOL = Rotary Potentiometer (Small) [maximum_resistance=100kΩ]
  SPK = Piezo Speaker
  Arduino1 = Arduino
  BTN3 = Pushbutton [package="[THT]"]
  BTN2 = Pushbutton [package="[THT]"]
  BTN1 = Pushbutton [package="[THT]"]
  R3 = Resistor [tolerance=±5% resistance=220 package=THT]
  R2 = Resistor [tolerance=±5% resistance=220 package=THT]
  LED3 = Pirahna Super Flux RGB LED (Oomlout)

nets:
  N1: LED1.Common_Anode, LED2.Common_Anode, Arduino1.+5V, LED3.Common_Anode
  N2: LED1.Red_Cathode, R1.Pin_0
  N3: LED1.Blue_Cathode, R3.Pin_0
  N4: LED1.Green_Cathode, R2.Pin_0
  N5: LED2.Red_Cathode, R7.Pin_0
  N6: LED2.Blue_Cathode, R9.Pin_0
  N7: LED2.Green_Cathode, R8.Pin_0
  N8: R1.Pin_1, Arduino1.D4
  N9: R4.Pin_0, LED3.Red_Cathode
  N10: R4.Pin_1, Arduino1.D9
  N11: R5.Pin_0, LED3.Green_Cathode
  N12: R5.Pin_1, Arduino1.D10
  N13: R6.Pin_0, LED3.Blue_Cathode
  N14: R6.Pin_1, Arduino1.D11
  N15: R7.Pin_1, Arduino1.A0
  N16: R8.Pin_1, Arduino1.A1
  N17: R9.Pin_1, Arduino1.A2
  N18: VOL.leg1, SPK.pin1, Arduino1.GND, BTN3.Pin_3, BTN3.Pin_4, BTN2.Pin_3, BTN2.Pin_4, BTN1.Pin_3, BTN1.Pin_4
  N19: VOL.wiper, SPK.pin2
  N20: VOL.leg2, Arduino1.D3
  N21: Arduino1.D12, BTN3.Pin_1, BTN3.Pin_2
  N22: Arduino1.D8, BTN2.Pin_1, BTN2.Pin_2
  N23: Arduino1.D7, BTN1.Pin_1, BTN1.Pin_2
  N24: Arduino1.D6, R3.Pin_1
  N25: Arduino1.D5, R2.Pin_1

notes:
  Sleepduino Shield v0.1
  gareth.halfacree.co.uk
  twitter.com/ghalfacree

custom parts:
  Pirahna Super Flux RGB LED (Oomlout): A full color SuperFlux LED.
