# Fritzing sketch macrokeyboard (saved by Fritzing 0.7.9b)
breadboards: 1

parts:
  part = Arduino  # not connected
  Leonardo = Arduino
  S1 = Pushbutton [package="[SMD]"]
  S2 = Pushbutton [package="[SMD]"]
  S3 = Pushbutton [package="[SMD]"]
  S4 = Pushbutton [package="[SMD]"]

nets:
  N1: Leonardo.GND, S1.Pin_2, S2.Pin_2, S3.Pin_2, S4.Pin_1, S4.Pin_2
  N2: Leonardo.D5, S4.Pin_3, S4.Pin_4
  N3: Leonardo.D4, S3.Pin_3, S3.Pin_4
  N4: Leonardo.D3, S2.Pin_3, S2.Pin_4
  N5: Leonardo.D2, S1.Pin_3, S1.Pin_4
