# Fritzing sketch weathermon_2 (saved by Fritzing 0.7.9b)
stripboards: 2

parts:
  part = BMP085 Breakout  # not connected
  BMP085 = BMP085 Breakout
  DHT22 = DHT22 Humidity and Temperature Sensor
  Arduino1 = Arduino

nets:
  VIN: BMP085.VIN, DHT22.VDD, Arduino1.+5V
  N1: BMP085.SCL, Arduino1.A5
  N2: BMP085.SDA, Arduino1.A4
  GND: BMP085.GND, DHT22.GND, Arduino1.GND
  N3: DHT22.DATA, Arduino1.A3

custom parts:
  BMP085 Breakout: A breakout for the BMP085 barometric pressure and temperature sensor
